// Logisim project Extra exercises.circ as structural Verilog: 2 circuits, main circuit T flip-flops
module T_flip_flops (
  output A,
  output B,
  output A_prime
);

  wire clock_1_out, t_ff_2_qn;

  Clock clock_1 (.out(clock_1_out));
  T_Flip_Flop t_ff_1 (.clk(clock_1_out), .T(t_ff_2_qn), .Q(A), .Qn(A_prime));  // open: preset, reset, en
  T_Flip_Flop t_ff_2 (.clk(clock_1_out), .T(clock_1_out), .Q(B), .Qn(t_ff_2_qn));  // open: preset, reset, en

  // Notes on the sheet:
  //   B'
endmodule

module D_flip_flops (
);

  wire and_1_out, and_2_out, clock_1_out, d_ff_1_q, d_ff_1_qn, d_ff_2_q, d_ff_2_qn, or_1_out;

  or or_1 (or_1_out, and_2_out, and_1_out);
  and and_1 (and_1_out, d_ff_1_qn, d_ff_2_qn);
  Clock clock_1 (.out(clock_1_out));
  and and_2 (and_2_out, d_ff_1_q, d_ff_2_q);
  D_Flip_Flop d_ff_1 (.clk(clock_1_out), .D(or_1_out), .Q(d_ff_1_q), .Qn(d_ff_1_qn));  // open: preset, en, reset
  D_Flip_Flop d_ff_2 (.clk(clock_1_out), .D(d_ff_2_qn), .Q(d_ff_2_q), .Qn(d_ff_2_qn));  // open: preset, en, reset

  // Notes on the sheet:
  //   A
  //   A'
  //   B
  //   B'
endmodule
