// Logisim project Game.circ as structural Verilog: 6 circuits, main circuit Level 1
module Level_1 (
  output out_1,
  output out_2
);

  wire B_qn, clock_1_out, j_k_ff_1_qn;

  Clock clock_1 (.out(clock_1_out));
  J_K_Flip_Flop j_k_ff_1 (
    .J(out_2), .clk(clock_1_out), .K(out_2), .Q(out_1), .Qn(j_k_ff_1_qn));  // open: preset, en, reset
  J_K_Flip_Flop B (.J(1'b1), .clk(clock_1_out), .K(1'b1), .Q(out_2), .Qn(B_qn));  // open: preset, en, reset

  // Notes on the sheet:
  //   Clock
  //   W1
  //   A
  //   A
  //   A'
  //   B
  //   B'
endmodule

module Level_2 (
  output out_1,
  output out_2,
  output out_3
);

  wire and_1_out, and_2_out, and_3_out, and_4_out, clock_1_out, or_1_out, or_2_out, or_3_out, t_ff_1_qn,
       t_ff_2_qn, t_ff_3_qn;

  or or_1 (or_1_out, and_1_out, and_2_out, and_3_out);
  or or_2 (or_2_out, and_1_out, and_4_out);
  Clock clock_1 (.out(clock_1_out));
  and and_1 (and_1_out, out_1, t_ff_2_qn, out_3);
  and and_2 (and_2_out, t_ff_1_qn, out_2);
  and and_3 (and_3_out, out_2, t_ff_3_qn);
  or or_3 (or_3_out, t_ff_1_qn, out_2, t_ff_3_qn);
  and and_4 (and_4_out, out_1, out_2, t_ff_3_qn);
  T_Flip_Flop t_ff_1 (.clk(clock_1_out), .T(or_1_out), .Q(out_1), .Qn(t_ff_1_qn));  // open: preset, reset, en
  T_Flip_Flop t_ff_2 (.clk(clock_1_out), .T(or_3_out), .Q(out_2), .Qn(t_ff_2_qn));  // open: preset, reset, en
  T_Flip_Flop t_ff_3 (.clk(clock_1_out), .T(or_2_out), .Q(out_3), .Qn(t_ff_3_qn));  // open: preset, reset, en

  // Notes on the sheet:
  //   O1
  //   O4
  //   O2
  //   O3
  //   A
  //   A'
  //   B'
  //   B
  //   C
  //   C'
endmodule

module Level_3 (
  output out_1,
  output out_2,
  output out_3,
  output out_4
);

  wire and_1_out, and_2_out, and_3_out, and_4_out, clock_1_out, d_ff_1_qn, d_ff_2_qn, d_ff_3_qn, d_ff_4_qn,
       or_1_out, or_2_out;

  or or_1 (or_1_out, and_3_out, and_4_out);
  and and_1 (and_1_out, d_ff_1_qn, d_ff_2_qn, out_3, out_4);
  and and_2 (and_2_out, d_ff_2_qn, d_ff_3_qn, out_4);
  Clock clock_1 (.out(clock_1_out));
  or or_2 (or_2_out, d_ff_1_qn, out_2, d_ff_3_qn, d_ff_4_qn);
  and and_3 (and_3_out, d_ff_1_qn, out_2, d_ff_3_qn, out_4);
  and and_4 (and_4_out, out_1, d_ff_2_qn, d_ff_3_qn, out_4);
  D_Flip_Flop d_ff_1 (.clk(clock_1_out), .D(or_1_out), .Q(out_1), .Qn(d_ff_1_qn));  // open: preset, en, reset
  D_Flip_Flop d_ff_2 (.clk(clock_1_out), .D(and_1_out), .Q(out_2), .Qn(d_ff_2_qn));  // open: preset, en, reset
  D_Flip_Flop d_ff_3 (.clk(clock_1_out), .D(and_2_out), .Q(out_3), .Qn(d_ff_3_qn));  // open: preset, en, reset
  D_Flip_Flop d_ff_4 (.clk(clock_1_out), .D(or_2_out), .Q(out_4), .Qn(d_ff_4_qn));  // open: preset, en, reset

  // Notes on the sheet:
  //   O2
  //   O3
  //   O4
  //   O1
  //   A
  //   A'
  //   B
  //   B'
  //   C
  //   C'
  //   D
  //   D'
endmodule

module Level_2_using_JK (
  output out_1,
  output out_2,
  output out_3
);

  wire and_1_out, clock_1_out, j_k_ff_1_qn, j_k_ff_2_qn, j_k_ff_3_qn, or_1_out, or_2_out, or_3_out, or_4_out,
       or_5_out;

  Clock clock_1 (.out(clock_1_out));
  or or_1 (or_1_out, out_2, out_1);
  or or_2 (or_2_out, j_k_ff_1_qn, out_3, out_2);
  or or_3 (or_3_out, j_k_ff_1_qn, out_2, j_k_ff_3_qn);
  and and_1 (and_1_out, out_1, out_2);
  or or_4 (or_4_out, and_1_out, out_3);
  or or_5 (or_5_out, out_1, j_k_ff_3_qn);
  J_K_Flip_Flop j_k_ff_1 (
    .J(or_1_out), .clk(clock_1_out), .K(or_2_out), .Q(out_1), .Qn(j_k_ff_1_qn));  // open: preset, en, reset
  J_K_Flip_Flop j_k_ff_2 (
    .J(or_3_out), .clk(clock_1_out), .K(clock_1_out), .Q(out_2), .Qn(j_k_ff_2_qn));  // open: preset, en, reset
  J_K_Flip_Flop j_k_ff_3 (
    .J(or_4_out), .clk(clock_1_out), .K(or_5_out), .Q(out_3), .Qn(j_k_ff_3_qn));  // open: preset, en, reset

  // Notes on the sheet:
  //   A
  //   A'
  //   B
  //   B'
  //   C
  //   C'
endmodule

module Level_2_using_D (
  output out_1,
  output out_2,
  output out_3
);

  wire and_1_out, and_2_out, and_3_out, and_4_out, and_5_out, and_6_out, clock_1_out, d_ff_1_qn, d_ff_2_qn,
       d_ff_3_qn, or_1_out, or_2_out, or_3_out;

  or or_1 (or_1_out, and_5_out, and_6_out);
  Clock clock_1 (.out(clock_1_out));
  or or_2 (or_2_out, and_1_out, and_2_out);
  or or_3 (or_3_out, and_3_out, and_4_out);
  and and_1 (and_1_out, d_ff_1_qn, out_2);
  and and_2 (and_2_out, out_1, d_ff_2_qn, d_ff_3_qn);
  and and_3 (and_3_out, d_ff_1_qn, d_ff_2_qn);
  and and_4 (and_4_out, d_ff_2_qn, d_ff_3_qn);
  and and_5 (and_5_out, out_1, out_2, d_ff_3_qn);
  and and_6 (and_6_out, d_ff_1_qn, out_3);
  D_Flip_Flop d_ff_1 (.clk(clock_1_out), .D(or_2_out), .Q(out_1), .Qn(d_ff_1_qn));  // open: preset, en, reset
  D_Flip_Flop d_ff_2 (.clk(clock_1_out), .D(or_3_out), .Q(out_2), .Qn(d_ff_2_qn));  // open: preset, en, reset
  D_Flip_Flop d_ff_3 (.clk(clock_1_out), .D(or_1_out), .Q(out_3), .Qn(d_ff_3_qn));  // open: preset, en, reset

  // Notes on the sheet:
  //   A
  //   A'
  //   B
  //   B'
  //   C
  //   C'
endmodule

module Level_3_using_T (
  output out_1,
  output out_2,
  output out_3,
  output out_4
);

  wire and_1_out, and_2_out, and_3_out, and_4_out, and_5_out, and_6_out, and_7_out, clock_1_out, or_1_out,
       or_2_out, or_3_out, t_ff_1_qn, t_ff_2_qn, t_ff_3_qn, t_ff_4_qn;

  or or_1 (or_1_out, and_1_out, and_2_out);
  or or_2 (or_2_out, and_3_out, and_4_out);
  or or_3 (or_3_out, and_6_out, and_7_out);
  Clock clock_1 (.out(clock_1_out));
  and and_1 (and_1_out, t_ff_1_qn, out_2, t_ff_3_qn, out_4);
  and and_2 (and_2_out, out_1, t_ff_2_qn, out_3, out_4);
  and and_3 (and_3_out, t_ff_1_qn, out_2, t_ff_3_qn, out_4);
  and and_4 (and_4_out, t_ff_1_qn, t_ff_2_qn, out_3, out_4);
  and and_5 (and_5_out, t_ff_2_qn, out_4);
  and and_6 (and_6_out, t_ff_1_qn, t_ff_2_qn, t_ff_3_qn, t_ff_4_qn);
  and and_7 (and_7_out, out_1, t_ff_2_qn, out_3, out_4);
  T_Flip_Flop t_ff_1 (.clk(clock_1_out), .T(or_1_out), .Q(out_1), .Qn(t_ff_1_qn));  // open: preset, reset, en
  T_Flip_Flop t_ff_2 (.clk(clock_1_out), .T(or_2_out), .Q(out_2), .Qn(t_ff_2_qn));  // open: preset, reset, en
  T_Flip_Flop t_ff_3 (.clk(clock_1_out), .T(and_5_out), .Q(out_3), .Qn(t_ff_3_qn));  // open: preset, reset, en
  T_Flip_Flop t_ff_4 (.clk(clock_1_out), .T(or_3_out), .Q(out_4), .Qn(t_ff_4_qn));  // open: preset, reset, en
endmodule
