// Logisim project JK_Synchronous_Circuit_0123 (1).circ as structural Verilog: 1 circuit, main circuit main
module main (
  output Q1,
  output Q0
);

  wire Clock_out;

  Clock Clock (.out(Clock_out));
  J_K_Flip_Flop JKB (.J(1'b1), .clk(Clock_out), .K(1'b1), .Q(Q0));  // open: Qn, preset, en, reset
  J_K_Flip_Flop JKA (.J(Q0), .clk(Clock_out), .K(Q0), .Q(Q1));  // open: Qn, preset, en, reset
endmodule
